// Logisim project pong_bot_proc.circ as structural Verilog: 8 circuits, main circuit main
module main (
  input  Start
);

  wire ball_x_1_bus_2, ball_y_1_bus_0, boarder_checker_1_nearpaddle_left, boarder_checker_1_nearpaddle_right,
       boarder_checker_1_reset, control_1_hit, Down_2_out, Down_out, UP_2_out, Up_out;
  wire [3:0] boarder_checker_1_score_left, boarder_checker_1_score_right;
  wire [15:0] ball_y_1_out, control_1_out_left, control_1_out_right, display_1_out_5, display_1_out_6,
       display_1_out_7, display_1_out_8, display_1_out_9, display_1_out_10, display_1_out_11,
       display_1_out_12, display_1_out_13, display_1_out_14, display_1_out_15, display_1_out_16,
       display_1_out_17, display_1_out_18, display_1_out_19, display_1_out_20, display_1_out_21,
       display_1_out_22, display_1_out_23, display_1_out_24, display_1_out_25, display_1_out_26,
       display_1_out_27, display_1_out_28, display_1_out_29, display_1_out_30, display_1_out_31,
       display_1_out_32, display_1_out_33, display_1_out_34, display_1_out_35, display_1_out_36;
  wire [31:0] ball_x_1_out;

  bot bot_1 (
    .coord_X(ball_x_1_out), .coord_Y(ball_y_1_out), .vel_Y(ball_y_1_bus_0), .vel_X(ball_x_1_bus_2));  // open: reset
  // Probe on ball_y_1_bus_0
  Ball_Y ball_y_1 (.Out(ball_y_1_out), .Reset(boarder_checker_1_reset), .hit(control_1_hit), .bus_0(ball_y_1_bus_0));
  Ball_X ball_x_1 (.Reset(boarder_checker_1_reset), .Out(ball_x_1_out), .hit(control_1_hit), .bus_2(ball_x_1_bus_2));
  // Probe on ball_x_1_bus_2
  Boarder_checker boarder_checker_1 (
    .Ball_X(ball_x_1_out), .NearPaddle_Right(boarder_checker_1_nearpaddle_right),
    .NearPaddle_Left(boarder_checker_1_nearpaddle_left), .Start(Start), .Reset(boarder_checker_1_reset),
    .Score_Right(boarder_checker_1_score_right), .Score_Left(boarder_checker_1_score_left));
  // Probe on ball_y_1_out
  Button Up (.out(Up_out));
  Button Down (.out(Down_out));
  Hex_Digit_Display hex_digit_display_1 (.value(boarder_checker_1_score_left));  // open: dp
  DotMatrix #(.matrixcols(32), .matrixrows(16)) dotmatrix_1 (
    .col0(display_1_out_5), .col1(display_1_out_21), .col2(display_1_out_6), .col3(display_1_out_22),
    .col4(display_1_out_7), .col5(display_1_out_23), .col6(display_1_out_8), .col7(display_1_out_24),
    .col8(display_1_out_9), .col9(display_1_out_25), .col10(display_1_out_10), .col11(display_1_out_26),
    .col12(display_1_out_11), .col13(display_1_out_27), .col14(display_1_out_12), .col15(display_1_out_28),
    .col16(display_1_out_13), .col17(display_1_out_29), .col18(display_1_out_14), .col19(display_1_out_30),
    .col20(display_1_out_15), .col21(display_1_out_31), .col22(display_1_out_16), .col23(display_1_out_32),
    .col24(display_1_out_17), .col25(display_1_out_33), .col26(display_1_out_18), .col27(display_1_out_34),
    .col28(display_1_out_19), .col29(display_1_out_35), .col30(display_1_out_20), .col31(display_1_out_36));
  Control control_1 (
    .Up_Left(Up_out), .Up_Right(UP_2_out), .Down_Left(Down_out), .Down_Right(Down_2_out),
    .hit(control_1_hit), .out_Left(control_1_out_left), .out_Right(control_1_out_right),
    .nearPaddle_Left(boarder_checker_1_nearpaddle_left), .Reset(boarder_checker_1_reset),
    .in_8(ball_y_1_out), .nearPaddle_Right(boarder_checker_1_nearpaddle_right));
  Button UP_2 (.out(UP_2_out));
  Button Down_2 (.out(Down_2_out));
  Display display_1 (
    .Ball_Y(ball_y_1_out), .BallX(ball_x_1_out), .out_5(display_1_out_5), .out_21(display_1_out_21),
    .out_6(display_1_out_6), .out_22(display_1_out_22), .out_7(display_1_out_7), .out_23(display_1_out_23),
    .out_8(display_1_out_8), .out_24(display_1_out_24), .out_9(display_1_out_9), .out_25(display_1_out_25),
    .out_10(display_1_out_10), .out_26(display_1_out_26), .out_11(display_1_out_11),
    .out_27(display_1_out_27), .out_12(display_1_out_12), .out_28(display_1_out_28),
    .out_13(display_1_out_13), .out_29(display_1_out_29), .out_14(display_1_out_14),
    .out_30(display_1_out_30), .out_15(display_1_out_15), .out_31(display_1_out_31),
    .out_16(display_1_out_16), .out_32(display_1_out_32), .out_17(display_1_out_17),
    .out_33(display_1_out_33), .out_18(display_1_out_18), .out_34(display_1_out_34),
    .out_19(display_1_out_19), .out_35(display_1_out_35), .out_20(display_1_out_20),
    .out_36(display_1_out_36), .Paddle_Left(control_1_out_left), .Paddle_Right(control_1_out_right));
  Hex_Digit_Display hex_digit_display_2 (.value(boarder_checker_1_score_right));  // open: dp
endmodule

module Ball_X (
  input  Reset,
  input  hit,
  output [31:0] Out,
  output bus_2
);

  wire Clk_out, comparator_1_eq, comparator_2_eq, DirectionX_out, multiplexer_1_out, not_1_out, or_1_out;
  wire [0:0] xor_1_out;
  wire [4:0] adder_1_out, multiplexer_2_out, register_2_q, subtractor_1_out;

  Random #(.width(1)) DirectionX (.clk(Clk_out), .next(1'b1), .out(DirectionX_out), .clr(1'b0));
  not not_1 (not_1_out, bus_2);
  Multiplexer #(.select(2), .enable("false")) multiplexer_1 (
    .in0(not_1_out), .in1(DirectionX_out), .in2(bus_2), .in3(bus_2), .out(multiplexer_1_out),
    .sel({1'b0, Reset}));
  Register #(.width(1)) register_1 (.D(multiplexer_1_out), .en(or_1_out), .Q(bus_2), .clk(Clk_out), .clr(1'b0));
  xor xor_1 (xor_1_out[0], bus_2, or_1_out);
  Multiplexer #(.select(2), .width(5), .enable("false")) multiplexer_2 (
    .in0(adder_1_out), .in1(subtractor_1_out), .in2(5'b01111), .in3(5'b01111), .out(multiplexer_2_out),
    .sel({Reset, xor_1_out[0]}));
  Clock Clk (.out(Clk_out));
  Register #(.width(5)) register_2 (.D(multiplexer_2_out), .en(1'b1), .Q(register_2_q), .clk(Clk_out));  // open: clr
  or or_1 (or_1_out, comparator_2_eq, comparator_1_eq, hit, Reset);
  Subtractor #(.width(5)) subtractor_1 (.a(register_2_q), .b(5'b00001), .out(subtractor_1_out));  // open: bin, bout
  Adder #(.width(5)) adder_1 (.a(register_2_q), .b(5'b00001), .out(adder_1_out));  // open: cin, cout
  Comparator #(.width(5)) comparator_1 (.a({5{1'b1}}), .b(register_2_q), .eq(comparator_1_eq));  // open: gt, lt
  Comparator #(.width(5)) comparator_2 (.a({5{1'b0}}), .b(register_2_q), .eq(comparator_2_eq));  // open: gt, lt
  Shifter #(.width(32)) shifter_1 (.in(32'h1), .\dist (register_2_q), .out(Out));

  // Notes on the sheet:
  //   X Position is the absysse coordinate
  //   Init X position for Ball
  //   Init value. 1 will make ball goes right, 0 will make it left
endmodule

module Ball_Y (
  input  hit,
  input  Reset,
  output [15:0] Out,
  output bus_0
);

  wire Clk_out, comparator_1_eq, comparator_2_eq, multiplexer_1_out, not_1_out, or_1_out, random_2_out;
  wire [0:0] xor_1_out;
  wire [3:0] adder_1_out, multiplexer_2_out, random_1_out, register_2_q, subtractor_1_out;

  Random #(.width(4), .seed(1)) random_1 (.clk(Clk_out), .next(1'b1), .out(random_1_out), .clr(1'b0));
  Random #(.width(1), .seed(1)) random_2 (.clk(Clk_out), .next(1'b1), .out(random_2_out), .clr(1'b0));
  not not_1 (not_1_out, bus_0);
  Multiplexer #(.select(2), .enable("false")) multiplexer_1 (
    .in0(not_1_out), .in1(random_2_out), .in2(bus_0), .in3(bus_0), .out(multiplexer_1_out), .sel({hit, Reset}));
  Register #(.width(1)) register_1 (.D(multiplexer_1_out), .en(or_1_out), .Q(bus_0), .clk(Clk_out), .clr(Reset));
  Multiplexer #(.select(2), .width(4), .enable("false")) multiplexer_2 (
    .in0(adder_1_out), .in1(subtractor_1_out), .in2(random_1_out), .in3(random_1_out),
    .out(multiplexer_2_out), .sel({Reset, xor_1_out[0]}));
  xor xor_1 (xor_1_out[0], bus_0, or_1_out);
  Clock Clk (.out(Clk_out));
  Register #(.width(4)) register_2 (.D(multiplexer_2_out), .en(1'b1), .Q(register_2_q), .clk(Clk_out), .clr(1'b0));
  or or_1 (or_1_out, comparator_2_eq, comparator_1_eq, comparator_1_eq);
  Subtractor #(.width(4)) subtractor_1 (.a(register_2_q), .b(4'b0001), .out(subtractor_1_out));  // open: bin, bout
  Adder #(.width(4)) adder_1 (.a(register_2_q), .b(4'b0001), .out(adder_1_out));  // open: cin, cout
  Comparator #(.width(4)) comparator_1 (.a(4'b1111), .b(register_2_q), .eq(comparator_1_eq));  // open: gt, lt
  Comparator #(.width(4)) comparator_2 (.a(4'b0000), .b(register_2_q), .eq(comparator_2_eq));  // open: gt, lt
  Shifter #(.width(16)) shifter_1 (.in(16'h1), .\dist (register_2_q), .out(Out));

  // Notes on the sheet:
  //   Max position ordinate
  //   Random Y position at reset
  //   Compute  + or - for the next coordinate.
  //   Select reset or + or -
  //   Y  touched a boundary or hit a paddle
  //   Boundary check when Y reaches 15 or 0
endmodule

module Paddle_1 (
  input  Button_Down,
  input  Button_UP,
  input  Reset,
  input  [15:0] Ball_y,
  input  NearPAddle,
  output [15:0] Out,
  output Hit
);

  wire and_1_out, and_2_out, bit_extender_1_out, bit_extender_2_out, bit_extender_3_out, bit_extender_4_out,
       bit_extender_5_out, bit_extender_6_out, bit_extender_7_out, bit_extender_8_out, bit_extender_9_out,
       bit_extender_10_out, bit_extender_11_out, bit_extender_12_out, bit_extender_13_out,
       bit_extender_14_out, bit_extender_15_out, bit_extender_16_out, clock_1_out, comparator_1_eq,
       comparator_2_eq, or_1_out, or_2_out;
  wire [3:0] adder_1_out, multiplexer_1_out, multiplexer_2_out, multiplexer_3_out, register_1_q,
       subtractor_1_out;
  wire [15:0] and_3_out, and_4_out, and_5_out, and_6_out, and_7_out, and_8_out, and_9_out, and_10_out,
       and_11_out, and_12_out, and_13_out, and_14_out, and_15_out, and_16_out, and_17_out, and_18_out,
       and_19_out, and_20_out, and_21_out, and_22_out, and_23_out, and_24_out, and_25_out, and_26_out,
       and_27_out, and_28_out, and_29_out, and_30_out, and_31_out, and_32_out, and_33_out, and_34_out,
       shifter_2_out, shifter_3_out, shifter_4_out, shifter_5_out, shifter_6_out, shifter_7_out,
       shifter_8_out, shifter_9_out, shifter_10_out, shifter_11_out, shifter_12_out, shifter_13_out,
       shifter_14_out, shifter_15_out, shifter_16_out;

  Subtractor #(.width(4)) subtractor_1 (.a(register_1_q), .b(4'b0001), .out(subtractor_1_out));  // open: bin, bout
  Adder #(.width(4)) adder_1 (.a(4'b0001), .b(register_1_q), .out(adder_1_out));  // open: cin, cout
  Multiplexer #(.select(2), .width(4), .enable("false")) multiplexer_1 (
    .in0(register_1_q), .in1(subtractor_1_out), .in2(adder_1_out), .in3(register_1_q),
    .out(multiplexer_1_out), .sel({Button_UP, Button_Down}));
  Multiplexer #(.width(4), .enable("false")) multiplexer_2 (
    .in0(multiplexer_3_out), .in1(4'b0101), .out(multiplexer_2_out), .sel(Reset));
  Clock clock_1 (.out(clock_1_out));
  Register #(.width(4)) register_1 (
    .D(multiplexer_2_out), .en(1'b1), .Q(register_1_q), .clk(clock_1_out));  // open: clr
  Comparator #(.width(4)) comparator_1 (.a(4'b1100), .b(adder_1_out), .eq(comparator_1_eq));  // open: gt, lt
  Comparator #(.width(4)) comparator_2 (.a(4'b1111), .b(subtractor_1_out), .eq(comparator_2_eq));  // open: gt, lt
  Multiplexer #(.width(4), .enable("false")) multiplexer_3 (
    .in0(multiplexer_1_out), .in1(register_1_q), .out(multiplexer_3_out), .sel(or_1_out));
  or or_1 (or_1_out, and_1_out, and_2_out);
  and and_1 (and_1_out, Button_Down, comparator_2_eq);
  Shifter #(.width(16)) shifter_1 (.in(16'h1f), .\dist (register_1_q), .out(Out));
  and and_2 (and_2_out, Button_UP, comparator_1_eq);
  assign and_3_out = Out & 16'h1;  // AND_Gate and_3, 16 bits wide
  assign and_4_out = Out & 16'h2;  // AND_Gate and_4, 16 bits wide
  assign and_5_out = Out & 16'h4;  // AND_Gate and_5, 16 bits wide
  assign and_6_out = Out & 16'h8;  // AND_Gate and_6, 16 bits wide
  assign and_7_out = Out & 16'h10;  // AND_Gate and_7, 16 bits wide
  assign and_8_out = Out & 16'h20;  // AND_Gate and_8, 16 bits wide
  assign and_9_out = Out & 16'h40;  // AND_Gate and_9, 16 bits wide
  assign and_10_out = Out & 16'h80;  // AND_Gate and_10, 16 bits wide
  assign and_11_out = Out & 16'h100;  // AND_Gate and_11, 16 bits wide
  assign and_12_out = Out & 16'h200;  // AND_Gate and_12, 16 bits wide
  assign and_13_out = Out & 16'h400;  // AND_Gate and_13, 16 bits wide
  assign and_14_out = Out & 16'h800;  // AND_Gate and_14, 16 bits wide
  assign and_15_out = Out & 16'h1000;  // AND_Gate and_15, 16 bits wide
  assign and_16_out = Out & 16'h2000;  // AND_Gate and_16, 16 bits wide
  assign and_17_out = Out & 16'h4000;  // AND_Gate and_17, 16 bits wide
  assign and_18_out = Out & 16'h8000;  // AND_Gate and_18, 16 bits wide
  assign and_19_out = and_3_out & Ball_y;  // AND_Gate and_19, 16 bits wide
  assign and_20_out = and_4_out & Ball_y;  // AND_Gate and_20, 16 bits wide
  assign and_21_out = and_5_out & Ball_y;  // AND_Gate and_21, 16 bits wide
  assign and_22_out = and_6_out & Ball_y;  // AND_Gate and_22, 16 bits wide
  assign and_23_out = and_7_out & Ball_y;  // AND_Gate and_23, 16 bits wide
  assign and_24_out = and_8_out & Ball_y;  // AND_Gate and_24, 16 bits wide
  assign and_25_out = and_9_out & Ball_y;  // AND_Gate and_25, 16 bits wide
  assign and_26_out = and_10_out & Ball_y;  // AND_Gate and_26, 16 bits wide
  assign and_27_out = and_11_out & Ball_y;  // AND_Gate and_27, 16 bits wide
  assign and_28_out = and_12_out & Ball_y;  // AND_Gate and_28, 16 bits wide
  assign and_29_out = and_13_out & Ball_y;  // AND_Gate and_29, 16 bits wide
  assign and_30_out = and_14_out & Ball_y;  // AND_Gate and_30, 16 bits wide
  assign and_31_out = and_15_out & Ball_y;  // AND_Gate and_31, 16 bits wide
  assign and_32_out = and_16_out & Ball_y;  // AND_Gate and_32, 16 bits wide
  assign and_33_out = and_17_out & Ball_y;  // AND_Gate and_33, 16 bits wide
  assign and_34_out = and_18_out & Ball_y;  // AND_Gate and_34, 16 bits wide
  Shifter #(.width(16), .shift("lr")) shifter_2 (.in(and_20_out), .\dist (4'b0001), .out(shifter_2_out));
  Shifter #(.width(16), .shift("lr")) shifter_3 (.in(and_21_out), .\dist (4'b0010), .out(shifter_3_out));
  Shifter #(.width(16), .shift("lr")) shifter_4 (.in(and_22_out), .\dist (4'b0011), .out(shifter_4_out));
  Shifter #(.width(16), .shift("lr")) shifter_5 (.in(and_23_out), .\dist (4'b0100), .out(shifter_5_out));
  Shifter #(.width(16), .shift("lr")) shifter_6 (.in(and_24_out), .\dist (4'b0101), .out(shifter_6_out));
  Shifter #(.width(16), .shift("lr")) shifter_7 (.in(and_25_out), .\dist (4'b0110), .out(shifter_7_out));
  Shifter #(.width(16), .shift("lr")) shifter_8 (.in(and_26_out), .\dist (4'b0111), .out(shifter_8_out));
  Shifter #(.width(16), .shift("lr")) shifter_9 (.in(and_27_out), .\dist (4'b1000), .out(shifter_9_out));
  Shifter #(.width(16), .shift("lr")) shifter_10 (.in(and_28_out), .\dist (4'b1001), .out(shifter_10_out));
  Shifter #(.width(16), .shift("lr")) shifter_11 (.in(and_29_out), .\dist (4'b1010), .out(shifter_11_out));
  Shifter #(.width(16), .shift("lr")) shifter_12 (.in(and_30_out), .\dist (4'b1011), .out(shifter_12_out));
  Shifter #(.width(16), .shift("lr")) shifter_13 (.in(and_31_out), .\dist (4'b1100), .out(shifter_13_out));
  Shifter #(.width(16), .shift("lr")) shifter_14 (.in(and_32_out), .\dist (4'b1101), .out(shifter_14_out));
  Shifter #(.width(16), .shift("lr")) shifter_15 (.in(and_33_out), .\dist (4'b1110), .out(shifter_15_out));
  Shifter #(.width(16), .shift("lr")) shifter_16 (.in(and_34_out), .\dist (4'b1111), .out(shifter_16_out));
  Bit_Extender #(.in_width(16), .out_width(1)) bit_extender_1 (.in(and_19_out), .out(bit_extender_1_out));
  Bit_Extender #(.in_width(16), .out_width(1)) bit_extender_2 (.in(shifter_2_out), .out(bit_extender_2_out));
  Bit_Extender #(.in_width(16), .out_width(1)) bit_extender_3 (.in(shifter_3_out), .out(bit_extender_3_out));
  Bit_Extender #(.in_width(16), .out_width(1)) bit_extender_4 (.in(shifter_4_out), .out(bit_extender_4_out));
  Bit_Extender #(.in_width(16), .out_width(1)) bit_extender_5 (.in(shifter_5_out), .out(bit_extender_5_out));
  Bit_Extender #(.in_width(16), .out_width(1)) bit_extender_6 (.in(shifter_6_out), .out(bit_extender_6_out));
  Bit_Extender #(.in_width(16), .out_width(1)) bit_extender_7 (.in(shifter_7_out), .out(bit_extender_7_out));
  Bit_Extender #(.in_width(16), .out_width(1)) bit_extender_8 (.in(shifter_8_out), .out(bit_extender_8_out));
  Bit_Extender #(.in_width(16), .out_width(1)) bit_extender_9 (.in(shifter_9_out), .out(bit_extender_9_out));
  Bit_Extender #(.in_width(16), .out_width(1)) bit_extender_10 (.in(shifter_10_out), .out(bit_extender_10_out));
  Bit_Extender #(.in_width(16), .out_width(1)) bit_extender_11 (.in(shifter_11_out), .out(bit_extender_11_out));
  Bit_Extender #(.in_width(16), .out_width(1)) bit_extender_12 (.in(shifter_12_out), .out(bit_extender_12_out));
  Bit_Extender #(.in_width(16), .out_width(1)) bit_extender_13 (.in(shifter_13_out), .out(bit_extender_13_out));
  Bit_Extender #(.in_width(16), .out_width(1)) bit_extender_14 (.in(shifter_14_out), .out(bit_extender_14_out));
  Bit_Extender #(.in_width(16), .out_width(1)) bit_extender_15 (.in(shifter_15_out), .out(bit_extender_15_out));
  Bit_Extender #(.in_width(16), .out_width(1)) bit_extender_16 (.in(shifter_16_out), .out(bit_extender_16_out));
  or or_2 (or_2_out, bit_extender_1_out, bit_extender_2_out, bit_extender_3_out, bit_extender_4_out, bit_extender_5_out, bit_extender_6_out, bit_extender_7_out, bit_extender_8_out, bit_extender_9_out, bit_extender_10_out, bit_extender_11_out, bit_extender_12_out, bit_extender_13_out, bit_extender_14_out, bit_extender_15_out, bit_extender_16_out);
  and Hit_paddle (Hit, or_2_out, NearPAddle);
endmodule

module Boarder_checker (
  input  Start,
  input  [31:0] Ball_X,
  output Reset,
  output NearPaddle_Right,
  output NearPaddle_Left,
  output [3:0] Score_Right,
  output [3:0] Score_Left
);

  wire comparator_1_eq, comparator_2_eq, comparator_5_eq, comparator_6_eq, Limit_Score_out, or_1_out,
       or_2_out;
  wire [3:0] adder_1_out, adder_2_out;

  Comparator #(.width(32)) comparator_1 (.a(32'h80000000), .b(Ball_X), .eq(comparator_1_eq));  // open: gt, lt
  Comparator #(.width(32)) comparator_2 (.a(32'h1), .b(Ball_X), .eq(comparator_2_eq));  // open: gt, lt
  Comparator #(.width(32)) comparator_3 (.a(32'h40000000), .b(Ball_X), .eq(NearPaddle_Right));  // open: gt, lt
  Comparator #(.width(32)) comparator_4 (.a(32'h2), .b(Ball_X), .eq(NearPaddle_Left));  // open: gt, lt
  or or_1 (or_1_out, Start, Limit_Score_out);
  or or_2 (or_2_out, comparator_1_eq, comparator_2_eq);
  Register #(.width(4)) register_1 (.D(adder_1_out), .en(1'b1), .Q(Score_Right), .clk(comparator_2_eq), .clr(or_1_out));
  Register #(.width(4)) register_2 (.D(adder_2_out), .en(1'b1), .Q(Score_Left), .clk(comparator_1_eq), .clr(or_1_out));
  Adder #(.width(4)) adder_1 (.a(Score_Right), .b(4'b0001), .out(adder_1_out));  // open: cin, cout
  Adder #(.width(4)) adder_2 (.a(Score_Left), .b(4'b0001), .out(adder_2_out));  // open: cin, cout
  Comparator #(.width(4)) comparator_5 (.a(4'b1111), .b(Score_Right), .eq(comparator_5_eq));  // open: gt, lt
  Comparator #(.width(4)) comparator_6 (.a(4'b1111), .b(Score_Left), .eq(comparator_6_eq));  // open: gt, lt
  or Limit_Score (Limit_Score_out, comparator_5_eq, comparator_6_eq);
  or or_3 (Reset, Start, Limit_Score_out, or_2_out);

  // Notes on the sheet:
  //   Score Player Left
  //   Score Player Right
endmodule

module Display (
  input  [15:0] Paddle_Right,
  input  [15:0] Paddle_Left,
  input  [15:0] Ball_Y,
  input  [31:0] BallX,
  output [15:0] out_5,
  output [15:0] out_6,
  output [15:0] out_7,
  output [15:0] out_8,
  output [15:0] out_9,
  output [15:0] out_10,
  output [15:0] out_11,
  output [15:0] out_12,
  output [15:0] out_13,
  output [15:0] out_14,
  output [15:0] out_15,
  output [15:0] out_16,
  output [15:0] out_17,
  output [15:0] out_18,
  output [15:0] out_19,
  output [15:0] out_20,
  output [15:0] out_21,
  output [15:0] out_22,
  output [15:0] out_23,
  output [15:0] out_24,
  output [15:0] out_25,
  output [15:0] out_26,
  output [15:0] out_27,
  output [15:0] out_28,
  output [15:0] out_29,
  output [15:0] out_30,
  output [15:0] out_31,
  output [15:0] out_32,
  output [15:0] out_33,
  output [15:0] out_34,
  output [15:0] out_35,
  output [15:0] out_36
);

  wire [15:0] multiplexer_1_out, multiplexer_32_out;

  assign out_5 = Paddle_Left | multiplexer_1_out;  // OR_Gate or_1, 16 bits wide
  Multiplexer #(.width(16), .enable("false")) multiplexer_1 (
    .in0({16{1'b0}}), .in1(Ball_Y), .out(multiplexer_1_out), .sel(BallX[0]));
  Multiplexer #(.width(16), .enable("false")) multiplexer_2 (
    .in0({16{1'b0}}), .in1(Ball_Y), .out(out_21), .sel(BallX[1]));
  Multiplexer #(.width(16), .enable("false")) multiplexer_3 (
    .in0({16{1'b0}}), .in1(Ball_Y), .out(out_6), .sel(BallX[2]));
  Multiplexer #(.width(16), .enable("false")) multiplexer_4 (
    .in0({16{1'b0}}), .in1(Ball_Y), .out(out_22), .sel(BallX[3]));
  Multiplexer #(.width(16), .enable("false")) multiplexer_5 (
    .in0({16{1'b0}}), .in1(Ball_Y), .out(out_23), .sel(BallX[5]));
  Multiplexer #(.width(16), .enable("false")) multiplexer_6 (
    .in0({16{1'b0}}), .in1(Ball_Y), .out(out_7), .sel(BallX[4]));
  Multiplexer #(.width(16), .enable("false")) multiplexer_7 (
    .in0({16{1'b0}}), .in1(Ball_Y), .out(out_8), .sel(BallX[6]));
  Multiplexer #(.width(16), .enable("false")) multiplexer_8 (
    .in0({16{1'b0}}), .in1(Ball_Y), .out(out_24), .sel(BallX[7]));
  Multiplexer #(.width(16), .enable("false")) multiplexer_9 (
    .in0({16{1'b0}}), .in1(Ball_Y), .out(out_9), .sel(BallX[8]));
  Multiplexer #(.width(16), .enable("false")) multiplexer_10 (
    .in0({16{1'b0}}), .in1(Ball_Y), .out(out_25), .sel(BallX[9]));
  Multiplexer #(.width(16), .enable("false")) multiplexer_11 (
    .in0({16{1'b0}}), .in1(Ball_Y), .out(out_10), .sel(BallX[10]));
  Multiplexer #(.width(16), .enable("false")) multiplexer_12 (
    .in0({16{1'b0}}), .in1(Ball_Y), .out(out_26), .sel(BallX[11]));
  Multiplexer #(.width(16), .enable("false")) multiplexer_13 (
    .in0({16{1'b0}}), .in1(Ball_Y), .out(out_27), .sel(BallX[13]));
  Multiplexer #(.width(16), .enable("false")) multiplexer_14 (
    .in0({16{1'b0}}), .in1(Ball_Y), .out(out_11), .sel(BallX[12]));
  Multiplexer #(.width(16), .enable("false")) multiplexer_15 (
    .in0({16{1'b0}}), .in1(Ball_Y), .out(out_12), .sel(BallX[14]));
  Multiplexer #(.width(16), .enable("false")) multiplexer_16 (
    .in0({16{1'b0}}), .in1(Ball_Y), .out(out_28), .sel(BallX[15]));
  Multiplexer #(.width(16), .enable("false")) multiplexer_17 (
    .in0({16{1'b0}}), .in1(Ball_Y), .out(out_13), .sel(BallX[16]));
  Multiplexer #(.width(16), .enable("false")) multiplexer_18 (
    .in0({16{1'b0}}), .in1(Ball_Y), .out(out_29), .sel(BallX[17]));
  Multiplexer #(.width(16), .enable("false")) multiplexer_19 (
    .in0({16{1'b0}}), .in1(Ball_Y), .out(out_14), .sel(BallX[18]));
  Multiplexer #(.width(16), .enable("false")) multiplexer_20 (
    .in0({16{1'b0}}), .in1(Ball_Y), .out(out_30), .sel(BallX[19]));
  Multiplexer #(.width(16), .enable("false")) multiplexer_21 (
    .in0({16{1'b0}}), .in1(Ball_Y), .out(out_31), .sel(BallX[21]));
  Multiplexer #(.width(16), .enable("false")) multiplexer_22 (
    .in0({16{1'b0}}), .in1(Ball_Y), .out(out_15), .sel(BallX[20]));
  Multiplexer #(.width(16), .enable("false")) multiplexer_23 (
    .in0({16{1'b0}}), .in1(Ball_Y), .out(out_16), .sel(BallX[22]));
  Multiplexer #(.width(16), .enable("false")) multiplexer_24 (
    .in0({16{1'b0}}), .in1(Ball_Y), .out(out_32), .sel(BallX[23]));
  Multiplexer #(.width(16), .enable("false")) multiplexer_25 (
    .in0({16{1'b0}}), .in1(Ball_Y), .out(out_17), .sel(BallX[24]));
  Multiplexer #(.width(16), .enable("false")) multiplexer_26 (
    .in0({16{1'b0}}), .in1(Ball_Y), .out(out_33), .sel(BallX[25]));
  Multiplexer #(.width(16), .enable("false")) multiplexer_27 (
    .in0({16{1'b0}}), .in1(Ball_Y), .out(out_18), .sel(BallX[26]));
  Multiplexer #(.width(16), .enable("false")) multiplexer_28 (
    .in0({16{1'b0}}), .in1(Ball_Y), .out(out_34), .sel(BallX[27]));
  Multiplexer #(.width(16), .enable("false")) multiplexer_29 (
    .in0({16{1'b0}}), .in1(Ball_Y), .out(out_35), .sel(BallX[29]));
  Multiplexer #(.width(16), .enable("false")) multiplexer_30 (
    .in0({16{1'b0}}), .in1(Ball_Y), .out(out_19), .sel(BallX[28]));
  Multiplexer #(.width(16), .enable("false")) multiplexer_31 (
    .in0({16{1'b0}}), .in1(Ball_Y), .out(out_20), .sel(BallX[30]));
  assign out_36 = multiplexer_32_out | Paddle_Right;  // OR_Gate or_2, 16 bits wide
  Multiplexer #(.width(16), .enable("false")) multiplexer_32 (
    .in0({16{1'b0}}), .in1(Ball_Y), .out(multiplexer_32_out), .sel(BallX[31]));
endmodule

module Control (
  input  Up_Left,
  input  Up_Right,
  input  Down_Left,
  input  Down_Right,
  input  nearPaddle_Left,
  input  nearPaddle_Right,
  input  Reset,
  input  [15:0] in_8,
  output [15:0] out_Left,
  output [15:0] out_Right,
  output hit
);

  wire paddle_1_1_hit, paddle_1_2_hit;

  Paddle_1 paddle_1_1 (
    .Button_Down(Down_Left), .Button_UP(Up_Left), .Reset(Reset), .Ball_y(in_8), .Out(out_Left),
    .Hit(paddle_1_1_hit), .NearPAddle(nearPaddle_Left));
  Paddle_1 paddle_1_2 (
    .Button_Down(Down_Right), .Button_UP(Up_Right), .Reset(Reset), .Ball_y(in_8), .Out(out_Right),
    .Hit(paddle_1_2_hit), .NearPAddle(nearPaddle_Right));
  or or_1 (hit, paddle_1_2_hit, paddle_1_1_hit);

  // Notes on the sheet:
  //   Left
  //   Right
endmodule

module bot (
  input  reset,
  input  [15:0] coord_Y,
  input  vel_X,
  input  vel_Y,
  input  [31:0] coord_X
);

  wire cdm_8_1_p2, cdm_8_1_p4, cdm_8_1_p5, cdm_8_1_p6, cdm_8_1_p7, cdm_8_1_p8, cdm_8_1_p9, cl, code, data,
       I_Osel, in_out_prime, mem, nand_1_out, not_1_out, not_2_out, not_3_out, RAM;
  wire [3:0] I_Oadr;
  wire [4:0] bitfinder_1_index;
  wire [7:0] cdm_8_1_p12, cdm_8_1_p13, cdm_8_1_p14, controlled_buffer_2_out, I_Odat, transistor_2_out;
  wire [7:4] transistor_1_out;

  Pull_Resistor pull_resistor_1 (.node(code));
  Pull_Resistor pull_resistor_2 (.node(data));
  // Probe on cdm_8_1_p4
  // Probe on cdm_8_1_p2
  // Probe on cdm_8_1_p5
  Clock clock_1 (.out(cl));
  // Probe on cdm_8_1_p7
  // Probe on cdm_8_1_p8
  // Probe on cdm_8_1_p6
  and and_1 (I_Osel, not_1_out, cl, data);
  not not_1 (not_1_out, nand_1_out);
  and and_2 (RAM, nand_1_out, data);
  Transistor #(.\type ("n"), .width(8)) transistor_1 (.in(cdm_8_1_p12), .out({transistor_1_out, I_Oadr}), .gate(mem));
  Transistor #(.\type ("n"), .width(8)) transistor_2 (.in(cdm_8_1_p13), .out(transistor_2_out), .gate(mem));
  // CdM_8 cdm_8_1: pin names not known; wires that end beside it: cl, cdm_8_1_p2, reset, cdm_8_1_p4, cdm_8_1_p5, cdm_8_1_p6, cdm_8_1_p7, cdm_8_1_p8, cdm_8_1_p9, mem, in_out_prime, cdm_8_1_p12, cdm_8_1_p13, cdm_8_1_p14
  Transistor #(.\type ("n"), .width(8)) transistor_3 (.in(controlled_buffer_2_out), .out(cdm_8_1_p14), .gate(mem));
  nand nand_1 (nand_1_out, transistor_1_out[4], transistor_1_out[5], transistor_1_out[6], transistor_1_out[7]);
  Decoder decoder_1 (.out0(code), .out1(data), .sel(cdm_8_1_p9), .en(mem));
  assign I_Odat = not_2_out ? transistor_2_out : 8'bz;  // Controlled_Buffer controlled_buffer_1
  not not_2 (not_2_out, in_out_prime);
  assign controlled_buffer_2_out = in_out_prime ? I_Odat : 8'bz;  // Controlled_Buffer controlled_buffer_2
  Pull_Resistor pull_resistor_3 (.node(I_Oadr[0]));
  Pull_Resistor pull_resistor_4 (.node(I_Oadr[1]));
  Pull_Resistor pull_resistor_5 (.node(I_Oadr[2]));
  Pull_Resistor pull_resistor_6 (.node(I_Oadr[3]));
  Pull_Resistor pull_resistor_7 (.node(transistor_1_out[4]));
  Pull_Resistor pull_resistor_8 (.node(transistor_1_out[5]));
  Pull_Resistor pull_resistor_9 (.node(transistor_1_out[6]));
  Pull_Resistor pull_resistor_10 (.node(transistor_1_out[7]));
  ROM rom_1 (.addr({transistor_1_out, I_Oadr}), .data(I_Odat), .sel(code));
  RAM ram_1 (.addr({transistor_1_out, I_Oadr}), .data(I_Odat), .sel(RAM), .clk(cl), .ld(in_out_prime));  // open: clr
  // Probe on {transistor_1_out, I_Oadr}
  // Probe on I_Odat
  Transistor #(.\type ("n"), .width(8)) transistor_4 (.in(8'he2), .out({transistor_1_out, I_Oadr}), .gate(not_3_out));
  Transistor #(.\type ("n"), .width(8)) transistor_5 (.in({3'b000, bitfinder_1_index}), .out(I_Odat), .gate(not_3_out));
  not not_3 (not_3_out, mem);
  // Probe on {3'b000, bitfinder_1_index}
  BitFinder #(.width(32)) bitfinder_1 (.in(coord_X), .index(bitfinder_1_index));  // open: found
  Multiplexer multiplexer_1 ();  // open: in0, in1, out, sel, en
  Counter #(.width(1), .max('h1)) counter_1 ();  // open: load, D, count, Q, carry, clk, clr

  // Other names for the same wires on the sheet: rd_wr_prime = in_out_prime

  // Notes on the sheet:
  //   r1
  //   r2
  //   r0
  //   r3
  //   физическое прерывание по питанию через транзистор в месте где ресет и тактирование чтобы вся эта херня начинала работать только когда шарик летит вправо
  //   contents of rom_1 (hex, n*v repeats v):
  //   d0 e4 b0 d1 e2 b5 5 e4 e d2 f 72 eb 10 ee 0 d2 1e 38 0 5 e1 19 ee 0 d2 0 85 0 ed 23 14 8e ee 1c d3
  //   e3 bf f ed 2d 1a 8b ee 26 d3 e5 bf 1e d3 1f 3b d0 e1 a3 ee 0 d7 d4 165*0 1e
endmodule
