// Logisim project projectB.circ as structural Verilog: 7 circuits, main circuit main
module main (
);

  wire DOWN_2_out, DOWN_out, score_1_restart, \score_1_рядом_слева , \score_1_рядом_справа , temp_1_hit,
       UP_2_out, UP_out;
  wire [3:0] \score_1_счет_слева , \score_1_счет_справа ;
  wire [31:0] temp_1_outl, temp_1_outr, videocarta_1_out_5, videocarta_1_out_6, videocarta_1_out_7,
       videocarta_1_out_8, videocarta_1_out_9, videocarta_1_out_10, videocarta_1_out_11, videocarta_1_out_12,
       videocarta_1_out_13, videocarta_1_out_14, videocarta_1_out_15, videocarta_1_out_16,
       videocarta_1_out_17, videocarta_1_out_18, videocarta_1_out_19, videocarta_1_out_20,
       videocarta_1_out_21, videocarta_1_out_22, videocarta_1_out_23, videocarta_1_out_24,
       videocarta_1_out_25, videocarta_1_out_26, videocarta_1_out_27, videocarta_1_out_28,
       videocarta_1_out_29, videocarta_1_out_30, videocarta_1_out_31, videocarta_1_out_32,
       videocarta_1_out_33, videocarta_1_out_34, videocarta_1_out_35, videocarta_1_out_36, x_1_out, y_1_out;

  score score_1 (
    .restart(score_1_restart), .\рядом_справа (\score_1_рядом_справа ), .x(x_1_out),
    .\рядом_слева (\score_1_рядом_слева ), .\счет_справа (\score_1_счет_справа ),
    .\счет_слева (\score_1_счет_слева ));
  temp temp_1 (
    .upL(UP_out), .downL(DOWN_out), .\рядом_слева (\score_1_рядом_слева ), .outL(temp_1_outl),
    .reset(score_1_restart), .upR(UP_2_out), .downR(DOWN_2_out), .y(y_1_out),
    .\рядом_справа (\score_1_рядом_справа ), .outR(temp_1_outr), .hit(temp_1_hit));
  x x_1 (.hit(temp_1_hit), .reset(score_1_restart), .out(x_1_out));
  y y_1 (.hit(temp_1_hit), .reset(score_1_restart), .out(y_1_out));
  Button UP (.out(UP_out));
  Button DOWN (.out(DOWN_out));
  Button UP_2 (.out(UP_2_out));
  Button DOWN_2 (.out(DOWN_2_out));
  Hex_Digit_Display hex_digit_display_1 (.value(\score_1_счет_слева ));  // open: dp
  DotMatrix #(.matrixcols(32), .matrixrows(32)) dotmatrix_1 (
    .col0(videocarta_1_out_5), .col1(videocarta_1_out_6), .col2(videocarta_1_out_7),
    .col3(videocarta_1_out_8), .col4(videocarta_1_out_9), .col5(videocarta_1_out_10),
    .col6(videocarta_1_out_11), .col7(videocarta_1_out_12), .col8(videocarta_1_out_13),
    .col9(videocarta_1_out_14), .col10(videocarta_1_out_15), .col11(videocarta_1_out_16),
    .col12(videocarta_1_out_17), .col13(videocarta_1_out_18), .col14(videocarta_1_out_19),
    .col15(videocarta_1_out_20), .col16(videocarta_1_out_21), .col17(videocarta_1_out_22),
    .col18(videocarta_1_out_23), .col19(videocarta_1_out_24), .col20(videocarta_1_out_25),
    .col21(videocarta_1_out_26), .col22(videocarta_1_out_27), .col23(videocarta_1_out_28),
    .col24(videocarta_1_out_29), .col25(videocarta_1_out_30), .col26(videocarta_1_out_31),
    .col27(videocarta_1_out_32), .col28(videocarta_1_out_33), .col29(videocarta_1_out_34),
    .col30(videocarta_1_out_35), .col31(videocarta_1_out_36));
  videocarta videocarta_1 (
    .y(y_1_out), .x(x_1_out), .palka_left(temp_1_outl), .palka_right(temp_1_outr),
    .out_5(videocarta_1_out_5), .out_6(videocarta_1_out_6), .out_7(videocarta_1_out_7),
    .out_8(videocarta_1_out_8), .out_9(videocarta_1_out_9), .out_10(videocarta_1_out_10),
    .out_11(videocarta_1_out_11), .out_12(videocarta_1_out_12), .out_13(videocarta_1_out_13),
    .out_14(videocarta_1_out_14), .out_15(videocarta_1_out_15), .out_16(videocarta_1_out_16),
    .out_17(videocarta_1_out_17), .out_18(videocarta_1_out_18), .out_19(videocarta_1_out_19),
    .out_20(videocarta_1_out_20), .out_21(videocarta_1_out_21), .out_22(videocarta_1_out_22),
    .out_23(videocarta_1_out_23), .out_24(videocarta_1_out_24), .out_25(videocarta_1_out_25),
    .out_26(videocarta_1_out_26), .out_27(videocarta_1_out_27), .out_28(videocarta_1_out_28),
    .out_29(videocarta_1_out_29), .out_30(videocarta_1_out_30), .out_31(videocarta_1_out_31),
    .out_32(videocarta_1_out_32), .out_33(videocarta_1_out_33), .out_34(videocarta_1_out_34),
    .out_35(videocarta_1_out_35), .out_36(videocarta_1_out_36));
  Hex_Digit_Display hex_digit_display_2 (.value(\score_1_счет_справа ));  // open: dp
endmodule

module videocarta (
  input  [31:0] palka_left,
  input  [31:0] y,
  input  [31:0] x,
  input  [31:0] palka_right,
  output [31:0] out_5,
  output [31:0] out_6,
  output [31:0] out_7,
  output [31:0] out_8,
  output [31:0] out_9,
  output [31:0] out_10,
  output [31:0] out_11,
  output [31:0] out_12,
  output [31:0] out_13,
  output [31:0] out_14,
  output [31:0] out_15,
  output [31:0] out_16,
  output [31:0] out_17,
  output [31:0] out_18,
  output [31:0] out_19,
  output [31:0] out_20,
  output [31:0] out_21,
  output [31:0] out_22,
  output [31:0] out_23,
  output [31:0] out_24,
  output [31:0] out_25,
  output [31:0] out_26,
  output [31:0] out_27,
  output [31:0] out_28,
  output [31:0] out_29,
  output [31:0] out_30,
  output [31:0] out_31,
  output [31:0] out_32,
  output [31:0] out_33,
  output [31:0] out_34,
  output [31:0] out_35,
  output [31:0] out_36
);

  wire [31:0] multiplexer_1_out, multiplexer_32_out;

  Multiplexer #(.width(32), .enable("false")) multiplexer_1 (
    .in0({32{1'b0}}), .in1(y), .out(multiplexer_1_out), .sel(x[0]));
  Multiplexer #(.width(32), .enable("false")) multiplexer_2 (.in0({32{1'b0}}), .in1(y), .out(out_10), .sel(x[1]));
  Multiplexer #(.width(32), .enable("false")) multiplexer_3 (.in0({32{1'b0}}), .in1(y), .out(out_9), .sel(x[2]));
  Multiplexer #(.width(32), .enable("false")) multiplexer_4 (.in0({32{1'b0}}), .in1(y), .out(out_12), .sel(x[3]));
  Multiplexer #(.width(32), .enable("false")) multiplexer_5 (.in0({32{1'b0}}), .in1(y), .out(out_14), .sel(x[4]));
  Multiplexer #(.width(32), .enable("false")) multiplexer_6 (.in0({32{1'b0}}), .in1(y), .out(out_16), .sel(x[5]));
  Multiplexer #(.width(32), .enable("false")) multiplexer_7 (.in0({32{1'b0}}), .in1(y), .out(out_17), .sel(x[6]));
  Multiplexer #(.width(32), .enable("false")) multiplexer_8 (.in0({32{1'b0}}), .in1(y), .out(out_20), .sel(x[7]));
  Multiplexer #(.width(32), .enable("false")) multiplexer_9 (.in0({32{1'b0}}), .in1(y), .out(out_22), .sel(x[8]));
  Multiplexer #(.width(32), .enable("false")) multiplexer_10 (.in0({32{1'b0}}), .in1(y), .out(out_25), .sel(x[9]));
  Multiplexer #(.width(32), .enable("false")) multiplexer_11 (.in0({32{1'b0}}), .in1(y), .out(out_26), .sel(x[10]));
  Multiplexer #(.width(32), .enable("false")) multiplexer_12 (.in0({32{1'b0}}), .in1(y), .out(out_28), .sel(x[11]));
  Multiplexer #(.width(32), .enable("false")) multiplexer_13 (.in0({32{1'b0}}), .in1(y), .out(out_31), .sel(x[12]));
  Multiplexer #(.width(32), .enable("false")) multiplexer_14 (.in0({32{1'b0}}), .in1(y), .out(out_32), .sel(x[13]));
  Multiplexer #(.width(32), .enable("false")) multiplexer_15 (.in0({32{1'b0}}), .in1(y), .out(out_34), .sel(x[14]));
  Multiplexer #(.width(32), .enable("false")) multiplexer_16 (.in0({32{1'b0}}), .in1(y), .out(out_35), .sel(x[15]));
  assign out_6 = palka_left | multiplexer_1_out;  // OR_Gate or_1, 32 bits wide
  Multiplexer #(.width(32), .enable("false")) multiplexer_17 (.in0({32{1'b0}}), .in1(y), .out(out_5), .sel(x[16]));
  Multiplexer #(.width(32), .enable("false")) multiplexer_18 (.in0({32{1'b0}}), .in1(y), .out(out_7), .sel(x[17]));
  Multiplexer #(.width(32), .enable("false")) multiplexer_19 (.in0({32{1'b0}}), .in1(y), .out(out_8), .sel(x[18]));
  Multiplexer #(.width(32), .enable("false")) multiplexer_20 (.in0({32{1'b0}}), .in1(y), .out(out_11), .sel(x[19]));
  Multiplexer #(.width(32), .enable("false")) multiplexer_21 (.in0({32{1'b0}}), .in1(y), .out(out_13), .sel(x[20]));
  Multiplexer #(.width(32), .enable("false")) multiplexer_22 (.in0({32{1'b0}}), .in1(y), .out(out_15), .sel(x[21]));
  Multiplexer #(.width(32), .enable("false")) multiplexer_23 (.in0({32{1'b0}}), .in1(y), .out(out_18), .sel(x[22]));
  Multiplexer #(.width(32), .enable("false")) multiplexer_24 (.in0({32{1'b0}}), .in1(y), .out(out_19), .sel(x[23]));
  Multiplexer #(.width(32), .enable("false")) multiplexer_25 (.in0({32{1'b0}}), .in1(y), .out(out_21), .sel(x[24]));
  Multiplexer #(.width(32), .enable("false")) multiplexer_26 (.in0({32{1'b0}}), .in1(y), .out(out_23), .sel(x[25]));
  Multiplexer #(.width(32), .enable("false")) multiplexer_27 (.in0({32{1'b0}}), .in1(y), .out(out_24), .sel(x[26]));
  Multiplexer #(.width(32), .enable("false")) multiplexer_28 (.in0({32{1'b0}}), .in1(y), .out(out_27), .sel(x[27]));
  Multiplexer #(.width(32), .enable("false")) multiplexer_29 (.in0({32{1'b0}}), .in1(y), .out(out_29), .sel(x[28]));
  Multiplexer #(.width(32), .enable("false")) multiplexer_30 (.in0({32{1'b0}}), .in1(y), .out(out_30), .sel(x[29]));
  Multiplexer #(.width(32), .enable("false")) multiplexer_31 (.in0({32{1'b0}}), .in1(y), .out(out_33), .sel(x[30]));
  Multiplexer #(.width(32), .enable("false")) multiplexer_32 (
    .in0({32{1'b0}}), .in1(y), .out(multiplexer_32_out), .sel(x[31]));
  assign out_36 = multiplexer_32_out | palka_right;  // OR_Gate or_2, 32 bits wide
endmodule

module score (
  input  [31:0] x,
  output restart,
  output \рядом_справа ,
  output \рядом_слева ,
  output [3:0] \счет_справа ,
  output [3:0] \счет_слева 
);

  wire comparator_1_eq, comparator_2_eq, comparator_3_eq, comparator_4_eq, comparator_5_eq, comparator_6_eq,
       or_1_out, or_2_out, or_3_out, or_4_out;
  wire [3:0] adder_1_out, adder_2_out;

  or or_1 (or_1_out, 1'b0, or_2_out);
  Adder #(.width(4)) adder_1 (.a(\счет_справа ), .b(4'b0001), .out(adder_1_out));  // open: cin, cout
  Register #(.width(4)) register_1 (
    .D(adder_1_out), .en(1'b1), .Q(\счет_справа ), .clk(comparator_4_eq), .clr(or_1_out));
  Comparator #(.width(4)) comparator_1 (.a(\счет_справа ), .b(4'b1111), .eq(comparator_1_eq));  // open: gt, lt
  or or_2 (or_2_out, comparator_1_eq, comparator_2_eq);
  or or_3 (or_3_out, or_4_out, or_2_out);
  Adder #(.width(4)) adder_2 (.a(\счет_слева ), .b(4'b0001), .out(adder_2_out));  // open: cin, cout
  Comparator #(.width(4)) comparator_2 (.a(\счет_слева ), .b(4'b1111), .eq(comparator_2_eq));  // open: gt, lt
  Register #(.width(4)) register_2 (
    .D(adder_2_out), .en(1'b1), .Q(\счет_слева ), .clk(comparator_3_eq), .clr(or_1_out));
  Comparator #(.width(32)) comparator_3 (.a(x), .b(32'h80000000), .eq(comparator_3_eq));  // open: gt, lt
  Comparator #(.width(32)) comparator_4 (.a(x), .b(32'h1), .eq(comparator_4_eq));  // open: gt, lt
  Comparator #(.width(32)) comparator_5 (.a(x), .b(32'h40000000), .eq(comparator_5_eq));  // open: gt, lt
  Comparator #(.width(32)) comparator_6 (.a(x), .b(32'h2), .eq(comparator_6_eq));  // open: gt, lt
  or or_4 (or_4_out, comparator_3_eq, comparator_4_eq);
endmodule

module detect_hit___rocketka (
  input  Reset,
  input  \Вверх ,
  input  \Вниз ,
  input  [31:0] y,
  input  \рядом ,
  output [31:0] out,
  output \попал 
);

  wire _1, _2, _3, _4, and_22_out, and_31_out, bit_extender_5_out, bit_extender_6_out, bit_extender_7_out,
       bit_extender_8_out, bit_extender_9_out, bit_extender_10_out, bit_extender_11_out, bit_extender_12_out,
       bit_extender_13_out, bit_extender_14_out, bit_extender_15_out, bit_extender_16_out, clock_1_out,
       comparator_1_eq, comparator_2_eq, or_1_out, or_2_out;
  wire [4:0] adder_1_out, multiplexer_1_out, multiplexer_2_out, multiplexer_3_out, register_1_q,
       subtractor_1_out;
  wire [31:0] and_1_out, and_2_out, and_3_out, and_4_out, and_5_out, and_6_out, and_7_out, and_8_out,
       and_9_out, and_10_out, and_11_out, and_12_out, and_13_out, and_14_out, and_15_out, and_16_out,
       and_17_out, and_18_out, and_19_out, and_20_out, and_21_out, and_23_out, and_24_out, and_25_out,
       and_26_out, and_27_out, and_28_out, and_29_out, and_30_out, and_32_out, and_33_out, and_34_out,
       shifter_1_out, shifter_2_out, shifter_3_out, shifter_4_out, shifter_5_out, shifter_6_out,
       shifter_7_out, shifter_8_out, shifter_9_out, shifter_10_out, shifter_11_out, shifter_12_out,
       shifter_13_out, shifter_14_out, shifter_15_out;

  assign and_1_out = out & 32'h1;  // AND_Gate and_1, 32 bits wide
  Bit_Extender #(.in_width(32), .out_width(1)) bit_extender_1 (.in(and_4_out), .out(_1));
  Subtractor #(.width(5)) subtractor_1 (.a(register_1_q), .b(5'b00001), .out(subtractor_1_out));  // open: bin, bout
  Adder #(.width(5)) adder_1 (.a(register_1_q), .b(5'b00001), .out(adder_1_out));  // open: cin, cout
  assign and_2_out = out & 32'h4;  // AND_Gate and_2, 32 bits wide
  assign and_3_out = out & 32'h2;  // AND_Gate and_3, 32 bits wide
  assign and_4_out = and_1_out & y;  // AND_Gate and_4, 32 bits wide
  assign and_5_out = and_3_out & y;  // AND_Gate and_5, 32 bits wide
  Bit_Extender #(.in_width(32), .out_width(1)) bit_extender_2 (.in(shifter_2_out), .out(_2));
  assign and_6_out = out & 32'h10;  // AND_Gate and_6, 32 bits wide
  assign and_7_out = out & 32'h8;  // AND_Gate and_7, 32 bits wide
  assign and_8_out = and_2_out & y;  // AND_Gate and_8, 32 bits wide
  assign and_9_out = and_7_out & y;  // AND_Gate and_9, 32 bits wide
  Shifter #(.width(32), .shift("lr")) shifter_1 (.in(and_8_out), .\dist (5'b00010), .out(shifter_1_out));
  Shifter #(.width(32), .shift("lr")) shifter_2 (.in(and_5_out), .\dist (5'b00001), .out(shifter_2_out));
  Bit_Extender #(.in_width(32), .out_width(1)) bit_extender_3 (.in(shifter_1_out), .out(_3));
  Bit_Extender #(.in_width(32), .out_width(1)) bit_extender_4 (.in(shifter_4_out), .out(_4));
  assign and_10_out = out & 32'h40;  // AND_Gate and_10, 32 bits wide
  assign and_11_out = out & 32'h20;  // AND_Gate and_11, 32 bits wide
  assign and_12_out = and_6_out & y;  // AND_Gate and_12, 32 bits wide
  assign and_13_out = and_11_out & y;  // AND_Gate and_13, 32 bits wide
  Shifter #(.width(32), .shift("lr")) shifter_3 (.in(and_12_out), .\dist (5'b00100), .out(shifter_3_out));
  Shifter #(.width(32), .shift("lr")) shifter_4 (.in(and_9_out), .\dist (5'b00011), .out(shifter_4_out));
  Bit_Extender #(.in_width(32), .out_width(1)) bit_extender_5 (.in(shifter_3_out), .out(bit_extender_5_out));
  Comparator #(.width(5)) comparator_1 (.a(5'b01100), .b(adder_1_out), .eq(comparator_1_eq));  // open: gt, lt
  assign and_14_out = out & 32'h80;  // AND_Gate and_14, 32 bits wide
  assign and_15_out = out & 32'h100;  // AND_Gate and_15, 32 bits wide
  assign and_16_out = and_10_out & y;  // AND_Gate and_16, 32 bits wide
  assign and_17_out = and_14_out & y;  // AND_Gate and_17, 32 bits wide
  Shifter #(.width(32), .shift("lr")) shifter_5 (.in(and_16_out), .\dist (5'b00110), .out(shifter_5_out));
  Shifter #(.width(32), .shift("lr")) shifter_6 (.in(and_13_out), .\dist (5'b00101), .out(shifter_6_out));
  Bit_Extender #(.in_width(32), .out_width(1)) bit_extender_6 (.in(shifter_6_out), .out(bit_extender_6_out));
  Bit_Extender #(.in_width(32), .out_width(1)) bit_extender_7 (.in(shifter_5_out), .out(bit_extender_7_out));
  assign and_18_out = out & 32'h400;  // AND_Gate and_18, 32 bits wide
  assign and_19_out = out & 32'h200;  // AND_Gate and_19, 32 bits wide
  assign and_20_out = and_19_out & y;  // AND_Gate and_20, 32 bits wide
  assign and_21_out = and_15_out & y;  // AND_Gate and_21, 32 bits wide
  Shifter #(.width(32), .shift("lr")) shifter_7 (.in(and_21_out), .\dist (5'b01000), .out(shifter_7_out));
  Shifter #(.width(32), .shift("lr")) shifter_8 (.in(and_17_out), .\dist (5'b00111), .out(shifter_8_out));
  Bit_Extender #(.in_width(32), .out_width(1)) bit_extender_8 (.in(shifter_8_out), .out(bit_extender_8_out));
  Multiplexer #(.select(2), .width(5), .enable("false")) multiplexer_1 (
    .in0(register_1_q), .in1(subtractor_1_out), .in2(adder_1_out), .in3(register_1_q),
    .out(multiplexer_1_out), .sel({\Вверх , \Вниз }));
  and and_22 (and_22_out, \Вверх , comparator_1_eq);
  assign and_23_out = out & 32'h1000;  // AND_Gate and_23, 32 bits wide
  assign and_24_out = out & 32'h800;  // AND_Gate and_24, 32 bits wide
  assign and_25_out = and_24_out & y;  // AND_Gate and_25, 32 bits wide
  assign and_26_out = and_18_out & y;  // AND_Gate and_26, 32 bits wide
  Shifter #(.width(32), .shift("lr")) shifter_9 (.in(and_26_out), .\dist (5'b01010), .out(shifter_9_out));
  Shifter #(.width(32), .shift("lr")) shifter_10 (.in(and_20_out), .\dist (5'b01001), .out(shifter_10_out));
  Bit_Extender #(.in_width(32), .out_width(1)) bit_extender_9 (.in(shifter_7_out), .out(bit_extender_9_out));
  Bit_Extender #(.in_width(32), .out_width(1)) bit_extender_10 (.in(shifter_10_out), .out(bit_extender_10_out));
  or or_1 (or_1_out, _1, _2, _3, _4, bit_extender_5_out, bit_extender_6_out, bit_extender_7_out, bit_extender_8_out, bit_extender_9_out, bit_extender_10_out, bit_extender_12_out, bit_extender_11_out, bit_extender_13_out, bit_extender_14_out, bit_extender_15_out, bit_extender_16_out);
  Multiplexer #(.width(5), .enable("false")) multiplexer_2 (
    .in0(multiplexer_3_out), .in1(5'b00101), .out(multiplexer_2_out), .sel(Reset));
  Comparator #(.width(5)) comparator_2 (.a(5'b01111), .b(subtractor_1_out), .eq(comparator_2_eq));  // open: gt, lt
  assign and_27_out = out & 32'h4000;  // AND_Gate and_27, 32 bits wide
  assign and_28_out = out & 32'h2000;  // AND_Gate and_28, 32 bits wide
  assign and_29_out = and_23_out & y;  // AND_Gate and_29, 32 bits wide
  assign and_30_out = and_28_out & y;  // AND_Gate and_30, 32 bits wide
  Shifter #(.width(32), .shift("lr")) shifter_11 (.in(and_29_out), .\dist (5'b01100), .out(shifter_11_out));
  Shifter #(.width(32), .shift("lr")) shifter_12 (.in(and_25_out), .\dist (5'b01011), .out(shifter_12_out));
  Bit_Extender #(.in_width(32), .out_width(1)) bit_extender_11 (.in(shifter_12_out), .out(bit_extender_11_out));
  Bit_Extender #(.in_width(32), .out_width(1)) bit_extender_12 (.in(shifter_9_out), .out(bit_extender_12_out));
  and and_31 (and_31_out, \Вниз , comparator_2_eq);
  assign and_32_out = out & 32'h8000;  // AND_Gate and_32, 32 bits wide
  assign and_33_out = and_27_out & y;  // AND_Gate and_33, 32 bits wide
  assign and_34_out = and_32_out & y;  // AND_Gate and_34, 32 bits wide
  Shifter #(.width(32), .shift("lr")) shifter_13 (.in(and_33_out), .\dist (5'b01110), .out(shifter_13_out));
  Shifter #(.width(32), .shift("lr")) shifter_14 (.in(and_30_out), .\dist (5'b01101), .out(shifter_14_out));
  Bit_Extender #(.in_width(32), .out_width(1)) bit_extender_13 (.in(shifter_11_out), .out(bit_extender_13_out));
  and and_35 (\попал , or_1_out, \рядом );
  Multiplexer #(.width(5), .enable("false")) multiplexer_3 (
    .in0(multiplexer_1_out), .in1(register_1_q), .out(multiplexer_3_out), .sel(or_2_out));
  Register #(.width(5)) register_1 (
    .D(multiplexer_2_out), .en(1'b1), .Q(register_1_q), .clk(clock_1_out));  // open: clr
  Clock clock_1 (.out(clock_1_out));
  or or_2 (or_2_out, and_31_out, and_22_out);
  Shifter #(.width(32), .shift("lr")) shifter_15 (.in(and_34_out), .\dist (5'b01111), .out(shifter_15_out));
  Bit_Extender #(.in_width(32), .out_width(1)) bit_extender_14 (.in(shifter_14_out), .out(bit_extender_14_out));
  Bit_Extender #(.in_width(32), .out_width(1)) bit_extender_15 (.in(shifter_13_out), .out(bit_extender_15_out));
  Shifter #(.width(32)) shifter_16 (.in(32'h1), .\dist (register_1_q), .out(out));
  Bit_Extender #(.in_width(32), .out_width(1)) bit_extender_16 (.in(shifter_15_out), .out(bit_extender_16_out));
endmodule

module x (
  input  reset,
  input  hit,
  output [31:0] out
);

  wire clock_1_out, comparator_1_eq, comparator_2_eq, multiplexer_1_out, not_1_out, or_1_out, random_1_out,
       register_1_q;
  wire [0:0] xor_1_out;
  wire [4:0] adder_1_out, multiplexer_2_out, register_2_q, subtractor_1_out;

  Comparator #(.width(5)) comparator_1 (.a({5{1'b1}}), .b(register_2_q), .eq(comparator_1_eq));  // open: gt, lt
  Comparator #(.width(5)) comparator_2 (.a({5{1'b0}}), .b(register_2_q), .eq(comparator_2_eq));  // open: gt, lt
  or or_1 (or_1_out, comparator_1_eq, comparator_2_eq, hit, reset);
  Random #(.width(1)) random_1 (.next(1'b1), .out(random_1_out), .clr(1'b0));  // open: clk
  Register #(.width(1)) register_1 (
    .D(multiplexer_1_out), .en(or_1_out), .Q(register_1_q), .clk(clock_1_out), .clr(1'b0));
  Clock clock_1 (.out(clock_1_out));
  not not_1 (not_1_out, register_1_q);
  Multiplexer #(.select(2), .enable("false")) multiplexer_1 (
    .in0(not_1_out), .in1(random_1_out), .in2(register_1_q), .in3(register_1_q), .out(multiplexer_1_out),
    .sel({1'b0, reset}));
  xor xor_1 (xor_1_out[0], register_1_q, or_1_out);
  Shifter #(.width(32)) shifter_1 (.in(32'h1), .\dist (register_2_q), .out(out));
  Multiplexer #(.select(2), .width(5), .enable("false")) multiplexer_2 (
    .in0(subtractor_1_out), .in1(adder_1_out), .in2(5'b01111), .in3(5'b01111), .out(multiplexer_2_out));  // open: sel
  Register #(.width(5)) register_2 (
    .D(multiplexer_2_out), .en(1'b1), .Q(register_2_q), .clk(clock_1_out));  // open: clr
  Adder #(.width(5)) adder_1 (.a(register_2_q), .b(5'b00001), .out(adder_1_out));  // open: cin, cout
  Subtractor #(.width(5)) subtractor_1 (.a(register_2_q), .b(5'b00001), .out(subtractor_1_out));  // open: bin, bout
endmodule

module y (
  input  hit,
  input  reset,
  output [31:0] out
);

  wire clock_1_out, comparator_1_eq, comparator_2_eq, multiplexer_1_out, not_1_out, or_1_out, random_2_out,
       register_1_q;
  wire [0:0] xor_1_out;
  wire [4:0] adder_1_out, multiplexer_2_out, random_1_out, register_2_q, subtractor_1_out;

  not not_1 (not_1_out, register_1_q);
  Register #(.width(1)) register_1 (
    .D(multiplexer_1_out), .en(or_1_out), .Q(register_1_q), .clk(clock_1_out), .clr(reset));
  Multiplexer #(.select(2), .enable("false")) multiplexer_1 (
    .in0(not_1_out), .in1(random_2_out), .in2(register_1_q), .in3(register_1_q), .out(multiplexer_1_out),
    .sel({hit, reset}));
  xor xor_1 (xor_1_out[0], or_1_out, register_1_q);
  or or_1 (or_1_out, comparator_2_eq, comparator_2_eq, comparator_1_eq);
  Random #(.width(5), .seed(1)) random_1 (.clk(clock_1_out), .next(1'b1), .out(random_1_out), .clr(1'b0));
  Random #(.width(1), .seed(1)) random_2 (.clk(clock_1_out), .next(1'b1), .out(random_2_out), .clr(1'b0));
  Clock clock_1 (.out(clock_1_out));
  Multiplexer #(.select(2), .width(5), .enable("false")) multiplexer_2 (
    .in0(adder_1_out), .in1(subtractor_1_out), .in2(random_1_out), .in3(random_1_out),
    .out(multiplexer_2_out), .sel({reset, xor_1_out[0]}));
  Comparator #(.width(5)) comparator_1 (.a({5{1'b0}}), .b(register_2_q), .eq(comparator_1_eq));  // open: gt, lt
  Register #(.width(5)) register_2 (.D(multiplexer_2_out), .en(1'b1), .Q(register_2_q), .clk(clock_1_out), .clr(1'b0));
  Comparator #(.width(5)) comparator_2 (.a({5{1'b1}}), .b(register_2_q), .eq(comparator_2_eq));  // open: gt, lt
  Subtractor #(.width(5)) subtractor_1 (.a(register_2_q), .b(5'b00001), .out(subtractor_1_out));  // open: bin, bout
  Adder #(.width(5)) adder_1 (.a(register_2_q), .b(5'b00001), .out(adder_1_out));  // open: cin, cout
  Shifter #(.width(32)) shifter_1 (.in(32'h1), .\dist (register_2_q), .out(out));
endmodule

module temp (
  input  [31:0] y,
  input  upL,
  input  downL,
  input  downR,
  input  upR,
  input  \рядом_слева ,
  input  reset,
  output [31:0] outL,
  output \рядом_справа ,
  output [31:0] outR,
  output hit
);

  wire \detect_hit_rocketka_1_попал , \detect_hit_rocketka_2_попал ;

  detect_hit___rocketka detect_hit_rocketka_1 (
    .\Вверх (upL), .\Вниз (downL), .\рядом (\рядом_слева ), .out(outL), .Reset(reset), .y(y),
    .\попал (\detect_hit_rocketka_1_попал ));
  detect_hit___rocketka detect_hit_rocketka_2 (
    .\Вверх (upR), .\Вниз (downR), .\рядом (\рядом_справа ), .out(outR), .Reset(reset), .y(y),
    .\попал (\detect_hit_rocketka_2_попал ));
  or or_1 (hit, \detect_hit_rocketka_2_попал , \detect_hit_rocketka_1_попал );
endmodule
